# Fritzing sketch Wiring Diagram (saved by Fritzing 0.9.3b)
breadboards: 2

parts:
  Componente1 = Arduino Nano (Rev3.0)
  Componente2 = Motor Driver 1A Dual TB6612FNG
  LED1 = LED - 5mm [color="Green (555nm)" package="5 mm [THT]"]
  HC-SR04_Sensor_1 = HC-SR04 Ultrasonic Distance Sensor
  HC-SR04_Sensor_2 = HC-SR04 Ultrasonic Distance Sensor
  HC-SR04_Sensor_3 = HC-SR04 Ultrasonic Distance Sensor
  M2 = DC Motor  # not connected
  S1 = Pushbutton [package="[THT]"]
  R1 = Resistor [tolerance=±5% resistance=330 package="2010 [SMD]"]
  R2 = Resistor [tolerance=±5% resistance=330 package="2010 [SMD]"]
  J1 = Basic Servo
  C1 = Capacitor [package=cap-pth-small2]
  C2 = Capacitor [package=cap-pth-small2]
  Q1 = Basic FET P-Channel [package="TO220 [THT]"]
  R3 = Resistor [tolerance=±5% resistance=330 package=THT]
  R4 = Resistor [tolerance=±5% resistance=330 package=THT]  # not connected
  LED2 = smd LED [color="Blue (430nm)" package="0603 [SMD]"]
  LED3 = LED - 5mm [color="Red (633nm)" package="5 mm [THT]"]  # not connected

nets:
  GND: Componente1.GND, Componente2.STBY, HC-SR04_Sensor_1.GND, HC-SR04_Sensor_2.GND, HC-SR04_Sensor_3.GND
  N1: Componente1.D2, Componente2.AIN1
  N2: Componente1.D3, Componente2.PWMA
  N3: Componente1.D4, Componente2.AIN2
  N4: Componente1.D5, S1.Pin_1, S1.Pin_2, R1.Pin_1
  N5: Componente1.D6, J1.pulse
  N6: Componente1.D7, HC-SR04_Sensor_1.ECHO
  N7: Componente1.D8, HC-SR04_Sensor_1.TRIG
  N8: Componente1.D9, HC-SR04_Sensor_3.ECHO
  N9: Componente1.D10, HC-SR04_Sensor_3.TRIG
  N10: Componente1.D11/MOSI, HC-SR04_Sensor_2.TRIG
  N11: Componente1.D12/MISO, HC-SR04_Sensor_2.ECHO
  VIN: Componente1.VIN, Componente2.VCC
  N12: Componente1.D13/SCK, LED2.cathode
  N13: Componente2.GND, Componente2.VM, R2.Pin_0, C1.1, C1.2, C2.2, Q1.source
  N14: LED1.cathode, S1.Pin_3, S1.Pin_4, C2.1, Q1.gate
  N15: LED1.anode, R2.Pin_1
  VCC: HC-SR04_Sensor_1.VCC, HC-SR04_Sensor_2.VCC, HC-SR04_Sensor_3.VCC
  N16: R3.Pin_0, LED2.anode
